// Logisim project MIPS.circ as structural Verilog: 1 circuit, main circuit Init Check
module Init_Check (
  input  A0,
  input  A1,
  input  A2,
  input  A3,
  input  A4,
  input  A5,
  input  A6,
  input  A7,
  input  A8,
  input  A9,
  input  A10,
  input  A11,
  input  A12,
  input  A13,
  input  A14,
  input  A15,
  input  A16,
  input  A17,
  input  A18,
  input  A19,
  input  A20,
  input  A21,
  input  A22,
  input  A23,
  input  A24,
  input  A25,
  input  A26,
  input  A27,
  input  A28,
  input  A29,
  input  A30,
  input  A31,
  output out_33
);

  wire and_1_out, and_2_out, and_3_out, and_4_out, and_5_out, and_6_out, and_7_out, and_8_out, and_9_out,
       and_10_out, and_11_out, and_12_out, and_13_out, and_14_out, and_15_out, and_16_out, and_17_out,
       and_18_out, and_19_out, and_20_out, and_21_out, and_22_out, and_23_out, and_24_out, and_25_out,
       and_26_out, and_27_out, and_28_out, and_29_out, and_30_out;

  and and_1 (and_1_out, A0, A1);
  and and_2 (and_2_out, A2, A3);
  and and_3 (and_3_out, A4, A5);
  and and_4 (and_4_out, A6, A7);
  and and_5 (and_5_out, A8, A9);
  and and_6 (and_6_out, A10, A11);
  and and_7 (and_7_out, A12, A13);
  and and_8 (and_8_out, A14, A15);
  and and_9 (and_9_out, A16, A17);
  and and_10 (and_10_out, A18, A19);
  and and_11 (and_11_out, A20, A21);
  and and_12 (and_12_out, A22, A23);
  and and_13 (and_13_out, A24, A25);
  and and_14 (and_14_out, A26, A27);
  and and_15 (and_15_out, A28, A29);
  and and_16 (and_16_out, A30, A31);
  and and_17 (and_17_out, and_1_out, and_2_out);
  and and_18 (and_18_out, and_3_out, and_4_out);
  and and_19 (and_19_out, and_5_out, and_6_out);
  and and_20 (and_20_out, and_7_out, and_8_out);
  and and_21 (and_21_out, and_9_out, and_10_out);
  and and_22 (and_22_out, and_11_out, and_12_out);
  and and_23 (and_23_out, and_13_out, and_14_out);
  and and_24 (and_24_out, and_15_out, and_16_out);
  and and_25 (and_25_out, and_17_out, and_18_out);
  and and_26 (and_26_out, and_25_out, and_27_out);
  and and_27 (and_27_out, and_19_out, and_20_out);
  and and_28 (and_28_out, and_21_out, and_22_out);
  and and_29 (and_29_out, and_28_out, and_30_out);
  and and_30 (and_30_out, and_23_out, and_24_out);
  and and_31 (out_33, and_26_out, and_29_out);
endmodule
